// Logisim project branch-comp.circ as structural Verilog: 1 circuit, main circuit branch_comp
module branch_comp (
  input  [31:0] BrData1,
  input  [31:0] BrData2,
  input  BrUn,
  output BrEq,
  output BrLt
);

  wire BrEqS, BrEqU, BrLtS, BrLtU;

  Comparator #(.width(32)) comparator_1 (.a(BrData1), .b(BrData2), .eq(BrEqS));  // open: gt, lt
  Comparator #(.mode("unsigned"), .width(32)) comparator_2 (.a(BrData1), .b(BrData2), .eq(BrEqU));  // open: gt, lt
  Comparator #(.width(32)) comparator_3 (.a(BrData1), .b(BrData2), .lt(BrLtS));  // open: gt, eq
  Comparator #(.mode("unsigned"), .width(32)) comparator_4 (.a(BrData1), .b(BrData2), .lt(BrLtU));  // open: gt, eq
  Multiplexer multiplexer_1 (.in0(BrEqS), .in1(BrEqU), .out(BrEq), .sel(BrUn));
  Multiplexer multiplexer_2 (.in0(BrLtS), .in1(BrLtU), .out(BrLt), .sel(BrUn));

  // Notes on the sheet:
  //   INPUTS to your circuit
  //   DON'T CHANGE THE LOCATIONS OF THE INPUTS AND OUTPUTS!
  //   OUTPUT from your circuit
endmodule
