// Logisim project control-logic.circ as structural Verilog: 1 circuit, main circuit control_logic
module control_logic (
  input  [31:0] Instruction,
  input  BrEq,
  input  BrLt,
  output PCSel,
  output RegWEn,
  output [2:0] ImmSel,
  output BrUn,
  output ASel,
  output BSel,
  output [3:0] ALUSel,
  output MemWEn,
  output [1:0] WBSel
);

  wire and_10_out, and_11_out, and_12_out, and_13_out, and_16_out, and_17_out, and_18_out, and_19_out,
       and_23_out, and_24_out, and_27_out, Btype_PCSel, is_auipc, is_B_type, is_bgeu, is_bltu, is_I_type,
       is_J_type, is_jalr, is_load_inst, is_lui, is_mul, is_mulh, is_mulhu, is_R_type, is_S_type, is_sraType,
       is_sub, is_U_type, multiplexer_7_out, not_1_out, not_2_out, not_3_out, not_4_out, or_3_out, or_4_out,
       or_5_out, or_6_out, or_7_out, or_8_out, or_9_out, or_10_out;
  wire [1:0] multiplexer_8_out;
  wire [2:0] multiplexer_1_out, multiplexer_4_out, multiplexer_6_out, multiplexer_9_out;
  wire [3:0] bit_extender_1_out, bit_extender_2_out, ItypeSel, multiplexer_16_out, multiplexer_17_out,
       multiplexer_18_out, multiplexer_19_out, multiplexer_21_out, RtypeSel, special;

  or or_1 (is_U_type, is_lui, is_auipc);
  and and_1 (is_I_type, Instruction[0], Instruction[1], ~Instruction[2], ~Instruction[3], Instruction[4], ~Instruction[5], ~Instruction[6]);  // AND_Gate
  and and_2 (is_R_type, Instruction[0], Instruction[1], ~Instruction[2], ~Instruction[3], Instruction[4], Instruction[5], ~Instruction[6]);  // AND_Gate
  and and_3 (is_B_type, Instruction[0], Instruction[1], ~Instruction[2], ~Instruction[3], ~Instruction[4], Instruction[5], Instruction[6]);  // AND_Gate
  and and_4 (is_S_type, Instruction[0], Instruction[1], ~Instruction[2], ~Instruction[3], ~Instruction[4], Instruction[5], ~Instruction[6]);  // AND_Gate
  and and_5 (is_load_inst, Instruction[0], Instruction[1], ~Instruction[2], ~Instruction[3], ~Instruction[4], ~Instruction[5], ~Instruction[6]);  // AND_Gate
  and and_6 (is_J_type, Instruction[0], Instruction[1], Instruction[2], Instruction[3], ~Instruction[4], Instruction[5], Instruction[6]);  // AND_Gate
  and and_7 (is_auipc, Instruction[0], Instruction[1], Instruction[2], ~Instruction[3], Instruction[4], ~Instruction[5], ~Instruction[6]);  // AND_Gate
  and and_8 (is_lui, Instruction[0], Instruction[1], Instruction[2], ~Instruction[3], Instruction[4], Instruction[5], ~Instruction[6]);  // AND_Gate
  and and_9 (is_jalr, Instruction[0], Instruction[1], Instruction[2], ~Instruction[3], ~Instruction[4], Instruction[5], Instruction[6]);  // AND_Gate
  not not_1 (not_1_out, is_R_type);
  not not_2 (not_2_out, BrEq);
  not not_3 (not_3_out, BrLt);
  not not_4 (not_4_out, BrLt);
  and and_10 (and_10_out, ~Instruction[12], ~Instruction[13], ~Instruction[14]);  // AND_Gate
  and and_11 (and_11_out, ~Instruction[25], ~Instruction[26], ~Instruction[27], ~Instruction[28], ~Instruction[29], Instruction[30], ~Instruction[31]);  // AND_Gate
  and and_12 (and_12_out, Instruction[12], ~Instruction[13], Instruction[14]);  // AND_Gate
  and and_13 (and_13_out, ~Instruction[25], ~Instruction[26], ~Instruction[27], ~Instruction[28], ~Instruction[29], Instruction[30], ~Instruction[31]);  // AND_Gate
  Multiplexer #(.width(3)) multiplexer_1 (.in0(3'b111), .in1(3'b100), .out(multiplexer_1_out), .sel(is_J_type));
  Multiplexer multiplexer_2 (.in0(1'b0), .in1(1'b1), .out(BSel), .sel(not_1_out));
  Multiplexer #(.select(3)) multiplexer_3 (
    .in0(BrEq), .in1(not_2_out), .in4(BrLt), .in5(not_3_out), .in6(BrLt), .in7(not_4_out), .out(Btype_PCSel),
    .sel(Instruction[14:12]));  // open: in2, in3
  and and_14 (is_sub, is_R_type, and_10_out, and_11_out);
  and and_15 (is_sraType, and_12_out, and_13_out);
  or or_2 (RegWEn, is_I_type, is_load_inst, is_R_type, is_U_type, is_jalr, is_J_type);
  Multiplexer #(.width(3)) multiplexer_4 (
    .in0(multiplexer_1_out), .in1(3'b011), .out(multiplexer_4_out), .sel(is_U_type));
  Multiplexer multiplexer_5 (.in0(1'b0), .in1(1'b1), .out(ASel), .sel(or_3_out));
  or or_3 (or_3_out, is_B_type, is_auipc, is_J_type);
  Multiplexer #(.width(3)) multiplexer_6 (
    .in0(multiplexer_4_out), .in1(3'b010), .out(multiplexer_6_out), .sel(is_B_type));
  Multiplexer multiplexer_7 (.in0(1'b0), .in1(1'b1), .out(multiplexer_7_out), .sel(or_4_out));
  or or_4 (or_4_out, is_jalr, is_J_type);
  and and_16 (and_16_out, ~Instruction[12], ~Instruction[13], ~Instruction[14]);  // AND_Gate
  and and_17 (and_17_out, Instruction[25], ~Instruction[26], ~Instruction[27], ~Instruction[28], ~Instruction[29], ~Instruction[30], ~Instruction[31]);  // AND_Gate
  and and_18 (and_18_out, Instruction[12], ~Instruction[13], ~Instruction[14]);  // AND_Gate
  and and_19 (and_19_out, Instruction[25], ~Instruction[26], ~Instruction[27], ~Instruction[28], ~Instruction[29], ~Instruction[30], ~Instruction[31]);  // AND_Gate
  Multiplexer #(.width(2)) multiplexer_8 (.in0(2'b10), .in1(2'b00), .out(multiplexer_8_out), .sel(is_load_inst));
  and and_20 (is_mul, is_R_type, and_16_out, and_17_out);
  and and_21 (is_mulh, is_R_type, and_18_out, and_19_out);
  Multiplexer #(.width(3)) multiplexer_9 (
    .in0(multiplexer_6_out), .in1(3'b001), .out(multiplexer_9_out), .sel(is_S_type));
  Multiplexer multiplexer_10 (.in0(multiplexer_7_out), .in1(Btype_PCSel), .out(PCSel), .sel(is_B_type));
  Multiplexer #(.width(2)) multiplexer_11 (.in0(multiplexer_8_out), .in1(2'b01), .out(WBSel), .sel(or_5_out));
  or or_5 (or_5_out, is_I_type, is_lui, is_R_type);
  or or_6 (or_6_out, is_I_type, is_jalr, is_load_inst);
  or or_7 (or_7_out, is_bgeu, is_bltu);
  Multiplexer #(.width(3)) multiplexer_12 (.in0(multiplexer_9_out), .in1(3'b000), .out(ImmSel), .sel(or_6_out));
  and and_22 (BrUn, is_B_type, or_7_out);
  Multiplexer multiplexer_13 (.in0(1'b0), .in1(1'b1), .out(MemWEn), .sel(is_S_type));
  and and_23 (and_23_out, Instruction[12], Instruction[13], ~Instruction[14]);  // AND_Gate
  and and_24 (and_24_out, Instruction[12], Instruction[13], Instruction[14]);
  and and_25 (is_mulhu, is_R_type, and_23_out);
  and and_26 (is_bgeu, is_B_type, and_24_out);
  assign bit_extender_1_out = {{1{1'b0}}, Instruction[14:12]};  // Bit_Extender bit_extender_1
  assign bit_extender_2_out = {{1{1'b0}}, Instruction[14:12]};  // Bit_Extender bit_extender_2
  or or_8 (or_8_out, is_mulh, is_mul);
  Multiplexer #(.width(4)) multiplexer_14 (.in0(bit_extender_1_out), .in1(4'b1101), .out(ItypeSel), .sel(is_sraType));
  Multiplexer #(.width(4)) multiplexer_15 (.in0(bit_extender_2_out), .in1(special), .out(RtypeSel), .sel(or_9_out));
  or or_9 (or_9_out, or_8_out, is_mulhu, or_10_out);
  or or_10 (or_10_out, is_sub, is_sraType);
  and and_27 (and_27_out, ~Instruction[12], Instruction[13], Instruction[14]);  // AND_Gate
  Multiplexer #(.width(4)) multiplexer_16 (.in1(4'b1101), .out(multiplexer_16_out), .sel(is_sraType));  // open: in0
  and and_28 (is_bltu, is_B_type, and_27_out);
  Multiplexer #(.width(4)) multiplexer_17 (.in0(4'b0000), .in1(4'b0011), .out(multiplexer_17_out), .sel(is_lui));
  Multiplexer #(.width(4)) multiplexer_18 (
    .in0(multiplexer_16_out), .in1(4'b1011), .out(multiplexer_18_out), .sel(is_mulhu));
  Multiplexer #(.width(4)) multiplexer_19 (
    .in0(multiplexer_18_out), .in1(4'b1001), .out(multiplexer_19_out), .sel(is_mulh));
  Multiplexer #(.select(2), .width(4)) multiplexer_20 (
    .in0(multiplexer_17_out), .in1(RtypeSel), .in2(ItypeSel), .out(ALUSel), .sel({is_I_type, is_R_type}));  // open: in3
  Multiplexer #(.width(4)) multiplexer_21 (
    .in0(multiplexer_19_out), .in1(4'b1000), .out(multiplexer_21_out), .sel(is_mul));
  Multiplexer #(.width(4)) multiplexer_22 (.in0(multiplexer_21_out), .in1(4'b1100), .out(special), .sel(is_sub));

  // Other names for the same wires on the sheet: opcode[6:0] = Instruction[6:0]; rd[4:0] = Instruction[11:7];
  //   funct3[2:0] = Instruction[14:12]; rs1[4:0] = Instruction[19:15]; imm[11:0] = Instruction[31:20];
  //   rs2[4:0] = Instruction[24:20]; funct7[6:0] = Instruction[31:25]

  // Notes on the sheet:
  //   INPUTS to your circuit
  //   DON'T CHANGE THE LOCATIONS OF THE INPUTS AND OUTPUTS!
  //   OUTPUT from your circuit
  //   I类型特判
  //   R类型特判
endmodule
