// Logisim project cpu_single_cycle.circ as structural Verilog: 1 circuit, main circuit cpu
module cpu (
  input  clk,
  input  [31:0] Instruction,
  input  [31:0] MemReadData,
  output [31:0] MemAddress,
  output [31:0] ProgramCounter,
  output [31:0] ra,
  output [31:0] sp,
  output [31:0] t0,
  output [31:0] t1,
  output [31:0] t2,
  output [31:0] s0,
  output [31:0] s1,
  output [31:0] a0,
  output [3:0] MemWriteMask,
  output [31:0] MemWriteData,
  output [31:0] out_16,
  output [31:0] out_17,
  output [31:0] out_18,
  output [4:0] out_19
);

  wire ASel, BrEq, BrLt, BSel, control_logic_1_brun, is_auipc, is_lui, MemRW, PCSel, RegWEn;
  wire [1:0] WBSel;
  wire [2:0] ImmSel;
  wire [3:0] ALUSel;
  wire [31:0] adder_1_out, adder_2_out, adder_3_out, ALUResult_Modified, DataToReg, Immediate,
       multiplexer_1_out, ReadData1, ReadData2, WData;

  Adder #(.width(32)) adder_1 (.a(ProgramCounter), .b(32'h4), .out(adder_1_out));  // open: cin, cout
  Multiplexer #(.width(32)) multiplexer_1 (.in0(adder_1_out), .in1(MemAddress), .out(multiplexer_1_out), .sel(PCSel));
  Register #(.width(32)) PC (.D(multiplexer_1_out), .en(1'b1), .clk(clk), .Q(ProgramCounter));  // open: clr
  and and_1 (is_lui, Instruction[0], Instruction[1], Instruction[2], ~Instruction[3], Instruction[4], Instruction[5], ~Instruction[6]);  // AND_Gate
  and and_2 (is_auipc, Instruction[0], Instruction[1], Instruction[2], ~Instruction[3], Instruction[4], ~Instruction[5], ~Instruction[6]);  // AND_Gate
  Adder #(.width(32)) adder_2 (.a(ProgramCounter), .b(Immediate), .out(adder_2_out));  // open: cin, cout
  Multiplexer #(.width(32)) multiplexer_2 (.in0(MemAddress), .in1(Immediate), .out(ALUResult_Modified), .sel(is_lui));
  Multiplexer #(.width(32)) multiplexer_3 (
    .in0(MemAddress), .in1(adder_2_out), .out(ALUResult_Modified), .sel(is_auipc));
  control_logic control_logic_1 (
    .Instruction(Instruction), .BrEq(BrEq), .BrLt(BrLt), .PCSel(PCSel), .RegWEn(RegWEn), .ImmSel(ImmSel),
    .BrUn(control_logic_1_brun), .ASel(ASel), .BSel(BSel), .ALUSel(ALUSel), .MemWEn(MemRW), .WBSel(WBSel));
  regfile regfile_1 (
    .ReadIndex1(Instruction[19:15]), .ReadIndex2(Instruction[24:20]), .WriteIndex(Instruction[11:7]),
    .WriteData(WData), .RegWEn(RegWEn), .clk(clk), .ra(ra), .sp(sp), .t0(t0), .t1(t1), .t2(t2), .s0(s0),
    .s1(s1), .a0(a0), .ReadData1(ReadData1), .ReadData2(ReadData2));
  // imm_gen imm_gen_1: pin names not known; wires that end beside it: Instruction, ImmSel, Immediate
  alu alu_1 (.A(out_17), .B(out_16), .ALUSel(ALUSel), .ALUResult(MemAddress));
  branch_comp branch_comp_1 (
    .BrData1(ReadData1), .BrData2(ReadData2), .BrUn(control_logic_1_brun), .BrEq(BrEq), .BrLt(BrLt));
  Multiplexer #(.width(32)) multiplexer_4 (.in0(ReadData2), .in1(Immediate), .out(out_16), .sel(BSel));
  Multiplexer #(.width(32)) multiplexer_5 (.in0(ReadData1), .in1(ProgramCounter), .out(out_17), .sel(ASel));
  partial_store partial_store_1 (
    .Instruction(Instruction), .MemAddress(MemAddress), .DataFromReg(ReadData2), .MemRW(MemRW),
    .MemWriteMask(MemWriteMask), .DataToMem(MemWriteData));
  partial_load partial_load_1 (
    .Instruction(Instruction), .MemAddress(MemAddress), .DataFromMem(MemReadData), .DataToReg(DataToReg));  // open: B_WSel
  Multiplexer #(.select(2), .width(32)) multiplexer_6 (
    .in0(DataToReg), .in1(ALUResult_Modified), .in2(adder_3_out), .out(WData), .sel(WBSel));  // open: in3
  Adder #(.width(32)) adder_3 (.a(ProgramCounter), .b(32'h4), .out(adder_3_out));  // open: cin, cout

  assign out_18 = MemAddress;
  assign out_19 = Instruction[19:15];

  // Other names for the same wires on the sheet: ALUInputA[31:0] = out_17; ALUInputB[31:0] = out_16;
  //   ALUResult[31:0] = MemAddress; opcode[6:0] = Instruction[6:0]; rd[4:0] = Instruction[11:7];
  //   rs1[4:0] = Instruction[19:15]; rs2[4:0] = Instruction[24:20]

  // Notes on the sheet:
  //   To IMEM
  //   IMEM (do **NOT** move this)
  //   From IMEM
  //   Inputs/Outputs for testing. Do **NOT** move these.
  //   It is OK to move the PC, RegFile, ALU, MEM, Branch Comp, Imm Gen, Partial Load, Partial Store and Control Logic to wherever is most convenient for you when constructing your CPU, and to delete this text
  //   To DMEM
  //   DMEM (do **NOT** move this)
  //   From DMEM
endmodule
