// Logisim project partial-load.circ as structural Verilog: 1 circuit, main circuit partial_load
module partial_load (
  input  [31:0] Instruction,
  input  [31:0] MemAddress,
  input  [31:0] DataFromMem,
  output [31:0] DataToReg,
  output [1:0] B_WSel
);

  wire [7:0] Byte_Sel;
  wire [15:0] Word_Sel;
  wire [31:0] Byte, Word;

  Multiplexer #(.select(2), .width(8)) multiplexer_1 (
    .in0(DataFromMem[7:0]), .in1(DataFromMem[15:8]), .in2(DataFromMem[23:16]), .in3(DataFromMem[31:24]),
    .out(Byte_Sel), .sel(MemAddress[1:0]));
  Multiplexer #(.select(2), .width(16)) multiplexer_2 (
    .in0(DataFromMem[15:0]), .in1(DataFromMem[23:8]), .in2(DataFromMem[31:16]), .out(Word_Sel),
    .sel(MemAddress[1:0]));  // open: in3
  assign Byte = {{24{Byte_Sel[7]}}, Byte_Sel};  // Bit_Extender bit_extender_1
  assign Word = {{16{Word_Sel[15]}}, Word_Sel};  // Bit_Extender bit_extender_2
  Multiplexer #(.select(2), .width(32)) multiplexer_3 (
    .in0(Byte), .in1(Word), .in2(DataFromMem), .out(DataToReg), .sel(Instruction[13:12]));  // open: in3

  assign B_WSel = MemAddress[1:0];

  // Other names for the same wires on the sheet: Byte0[7:0] = DataFromMem[7:0]; HalfWord0[15:0] = DataFromMem[15:0];
  //   Byte1[7:0] = DataFromMem[15:8]; HalfWord1[15:0] = DataFromMem[23:8]; Byte2[7:0] = DataFromMem[23:16];
  //   HalfWord2[15:0] = DataFromMem[31:16]; Byte3[7:0] = DataFromMem[31:24]; funct3_lower2[1:0] = Instruction[13:12]

  // Notes on the sheet:
  //   INPUTS to your circuit
  //   DON'T CHANGE THE LOCATIONS OF THE INPUTS AND OUTPUTS!
  //   OUTPUT from your circuit
endmodule
