// Logisim project partial-store.circ as structural Verilog: 1 circuit, main circuit partial_store
module partial_store (
  input  [31:0] Instruction,
  input  [31:0] MemAddress,
  input  [31:0] DataFromReg,
  input  MemRW,
  output [3:0] MemWriteMask,
  output [31:0] DataToMem
);

  wire [3:0] MemWriteMask_en, sb_mask, sh_mask;
  wire [31:0] Data_sb_ex, Data_sb_shift, Data_sh_ex, Data_sh_shift, shifter_1_out, shifter_2_out,
       shifter_3_out, shifter_4_out;

  Multiplexer #(.select(2), .width(4)) multiplexer_1 (
    .in0(sb_mask), .in1(sh_mask), .in2(4'b1111), .out(MemWriteMask_en), .sel(Instruction[13:12]));  // open: in3
  Multiplexer #(.width(4)) multiplexer_2 (.in0(4'b0000), .in1(MemWriteMask_en), .out(MemWriteMask), .sel(MemRW));
  assign Data_sb_ex = {{24{1'b0}}, DataFromReg[7:0]};  // Bit_Extender bit_extender_1
  assign Data_sh_ex = {{16{1'b0}}, DataFromReg[15:0]};  // Bit_Extender bit_extender_2
  Shifter #(.width(32)) shifter_1 (.in(Data_sh_ex), .\dist (5'b10000), .out(shifter_1_out));
  Shifter #(.width(32)) shifter_2 (.in(Data_sb_ex), .\dist (5'b01000), .out(shifter_2_out));
  Shifter #(.width(32)) shifter_3 (.in(Data_sb_ex), .\dist (5'b10000), .out(shifter_3_out));
  Multiplexer #(.select(2), .width(32)) multiplexer_3 (
    .in0(Data_sh_ex), .in2(shifter_1_out), .out(Data_sh_shift), .sel(MemAddress[1:0]));  // open: in1, in3
  Multiplexer #(.select(2), .width(32)) multiplexer_4 (
    .in0(Data_sb_ex), .in1(shifter_2_out), .in2(shifter_3_out), .in3(shifter_4_out), .out(Data_sb_shift),
    .sel(MemAddress[1:0]));
  Multiplexer #(.select(2), .width(4)) multiplexer_5 (
    .in0(4'b0001), .in1(4'b0010), .in2(4'b0100), .in3(4'b1000), .out(sb_mask), .sel(MemAddress[1:0]));
  Shifter #(.width(32)) shifter_4 (.in(Data_sb_ex), .\dist (5'b11000), .out(shifter_4_out));
  Multiplexer #(.select(2), .width(4)) multiplexer_6 (
    .in0(4'b0011), .in2(4'b1100), .out(sh_mask), .sel(MemAddress[1:0]));  // open: in1, in3
  Multiplexer #(.select(2), .width(32)) multiplexer_7 (
    .in0(Data_sb_shift), .in1(Data_sh_shift), .in2(DataFromReg), .out(DataToMem), .sel(Instruction[13:12]));  // open: in3

  // Other names for the same wires on the sheet: Data_sb[7:0] = DataFromReg[7:0]; Data_sh[15:0] = DataFromReg[15:0];
  //   Data_sw[31:0] = DataFromReg; funct3_lower2[1:0] = Instruction[13:12]; B_WSel[1:0] = MemAddress[1:0]

  // Notes on the sheet:
  //   INPUTS to your circuit
  //   DON'T CHANGE THE LOCATIONS OF THE INPUTS AND OUTPUTS!
  //   OUTPUT from your circuit
endmodule
